# Fritzing sketch 13_LCD1602 (saved by Fritzing 0.9.1b)
breadboards: 1

parts:
  LCD1 = LCD screen
  U1 = POT [package=alps_pot]
  Raspberry_Pi1 = Raspberry Pi B+

nets:
  VSS: LCD1.VSS, LCD1.R/W, LCD1.LED-, U1.E, Raspberry_Pi1.GND
  VDD: LCD1.VDD, LCD1.LED+, U1.A, Raspberry_Pi1.5V
  N1: LCD1.V0, U1.S
  N2: LCD1.RS, Raspberry_Pi1.GPIO14
  N3: LCD1.E, Raspberry_Pi1.GPIO15
  N4: LCD1.DB4, Raspberry_Pi1.GPIO17
  N5: LCD1.DB5, Raspberry_Pi1.GPIO18
  N6: LCD1.DB6, Raspberry_Pi1.GPIO27
  N7: LCD1.DB7, Raspberry_Pi1.GPIO22
