# Fritzing sketch 07_Motor (saved by Fritzing 0.9.2b)
circuit board: 8.46667cm x 5.64444cm
breadboards: 1

parts:
  IC1 = L293D [package=THT]
  M1 = DC Motor
  D1 = Rectifier Diode [part_number=1N4001 package="300 mil [THT]"]
  D2 = Rectifier Diode [part_number=1N4001 package="300 mil [THT]"]
  D3 = Rectifier Diode [part_number=1N4001 package="300 mil [THT]"]
  D4 = Rectifier Diode [part_number=1N4001 package="300 mil [THT]"]
  元件1 = Breadboard Power Supply Board SMD
  U1 = Optocoupler [package=THT]
  U2 = Optocoupler [package=THT]
  R1 = Resistor [tolerance=±5% resistance=220 package=THT]
  R3 = Resistor [tolerance=±5% resistance=10k package=THT]
  R4 = Resistor [tolerance=±5% resistance=10k package=THT]
  Raspberry_Pi1 = Raspberry Pi B+
  R2 = Resistor [tolerance=±5% resistance=220 package="2512 [SMD]"]

nets:
  N1: IC1.Enable_1, Raspberry_Pi1.GPIO27
  N2: IC1.In_1, U1.Pin_5, R3.Pin_1
  N3: IC1.Out_1_(_Controlled_by_Enable_1_), M1.pin_2, D1.anode, D2.cathode
  GND: IC1.0V, D2.anode, D4.anode, 元件1.GND, U1.Pin_4, U2.Pin_4, Raspberry_Pi1.GND
  N4: IC1.Out_2_(_Controlled_by_Enable_1_), M1.pin_1, D3.anode, D4.cathode
  N5: IC1.In_2, U2.Pin_5, R4.Pin_1
  N6: IC1.+Vmotor, IC1.+V, D1.cathode, D3.cathode, 元件1.VCC, R1.Pin_0, R3.Pin_0, R4.Pin_0, R2.Pin_0
  N7: U1.Pin_1, R2.Pin_1
  N8: U1.Pin_2, Raspberry_Pi1.GPIO18
  N9: U2.Pin_1, R1.Pin_1
  N10: U2.Pin_2, Raspberry_Pi1.GPIO17
